// Logisim project 4BitParity.circ as structural Verilog: 5 circuits, main circuit main
module main (
  input  Halt_Enable
);

  wire and_2_out, CLK, Correct, Done_Testing, Halt, Input, not_1_out, not_2_out, not_3_out, Solution,
       YourAnswer;
  wire [6:0] counter_1_q, TestNumber;

  not not_1 (not_1_out, Correct);
  Clock clock_1 (.out(CLK));
  and and_1 (Halt, Halt_Enable, not_1_out);
  Inputs inputs_1 (.Halt(Halt), .CLK(CLK), .Input(Input), .TestNumber(TestNumber), .Done_Testing(Done_Testing));
  _4BitEvenParity u_4bitevenparity_1 (.Input(Input), .CLK(CLK), .Is_Even(YourAnswer));
  // Probe on Input
  // Probe on YourAnswer
  // Probe on Solution
  // Probe on Correct
  not not_2 (not_2_out, Halt);
  and and_2 (and_2_out, Correct, not_2_out, not_3_out);
  not not_3 (not_3_out, Done_Testing);
  Checker checker_1 (.Your_Answer(YourAnswer), .TestNumber(TestNumber), .Correct(Correct), .Solution(Solution));
  Counter #(.width(7), .max('h41), .ongoal("stay")) counter_1 (
    .count(and_2_out), .Q(counter_1_q), .clk(CLK));  // open: load, D, carry, clr
  // Probe on counter_1_q

  // Notes on the sheet:
  //   Ardalan Emamjomehkashan 915356454 
  //   Faustine Yiu 913062973
  //   Max 65
endmodule

module _4BitEvenParity (
  input  Input,
  input  CLK,
  output Is_Even
);

  wire [3:0] parity_1_ap, register_1_q;

  Parity parity_1 (
    .A(register_1_q[0]), .B(register_1_q[1]), .C(register_1_q[2]), .D(register_1_q[3]), .IN(Input),
    .Ap(parity_1_ap[0]), .Bp(parity_1_ap[1]), .Cp(parity_1_ap[2]), .Dp(parity_1_ap[3]));
  Register #(.width(4)) register_1 (.D(parity_1_ap), .Q(register_1_q), .clk(CLK));  // open: en, clr
  // Probe on register_1_q
  and and_1 (Is_Even, register_1_q[0], register_1_q[1], register_1_q[2], register_1_q[3]);
endmodule

module Inputs (
  input  Halt,
  input  CLK,
  output Input,
  output [6:0] TestNumber,
  output Done_Testing
);

  wire not_1_out;

  not not_1 (not_1_out, Halt);
  Counter #(.width(7), .max('h41), .ongoal("stay")) counter_1 (
    .count(not_1_out), .Q(TestNumber), .carry(Done_Testing), .clk(CLK));  // open: load, D, clr
  ROM #(.addrWidth(7), .dataWidth(1)) rom_1 (.addr(TestNumber), .data(Input));  // open: sel

  // Notes on the sheet:
  //   contents of rom_1 (hex, n*v repeats v):
  //   7*0 1 0 0 1 0 0 0 1 1 0 1 0 0 0 1 0 1 0 1 1 0 0 4*1 0 0 0 1 0 0 1 1 0 1 0 1 0 4*1 0 0 1 1 0 4*1 0
  //   4*1
endmodule

module Checker (
  input  Your_Answer,
  input  [6:0] TestNumber,
  output Correct,
  output Solution
);

  ROM #(.addrWidth(7), .dataWidth(1)) rom_1 (.addr(TestNumber), .data(Solution));  // open: sel
  Comparator #(.width(1)) comparator_1 (.a(Solution), .b(Your_Answer), .eq(Correct));  // open: gt, lt

  // Notes on the sheet:
  //   contents of rom_1 (hex, n*v repeats v):
  //   4*0 1 11*0 1 7*0 1 0 0 0 1 11*0 1 0 0 0 1 7*0 1 11*0 1
endmodule

module Parity (
  input  A,
  input  B,
  input  C,
  input  D,
  input  IN,
  output Ap,
  output Bp,
  output Cp,
  output Dp
);

  wire and_1_out, and_2_out, and_3_out, and_4_out, and_5_out, and_6_out, and_7_out, and_8_out, and_9_out,
       and_10_out, and_11_out, and_12_out, and_13_out, and_14_out, and_15_out, and_16_out, and_17_out,
       and_18_out, not_1_out, not_2_out, not_3_out, not_4_out, not_5_out, not_6_out, not_7_out, not_8_out,
       not_9_out, not_10_out, not_11_out, not_12_out, not_13_out, not_14_out, not_15_out, not_16_out,
       not_17_out, not_18_out, not_19_out, not_20_out, not_21_out, not_22_out, not_23_out;

  not not_1 (not_1_out, B);
  not not_2 (not_2_out, D);
  not not_3 (not_3_out, A);
  not not_4 (not_4_out, IN);
  not not_5 (not_5_out, C);
  not not_6 (not_6_out, C);
  not not_7 (not_7_out, B);
  not not_8 (not_8_out, A);
  not not_9 (not_9_out, IN);
  not not_10 (not_10_out, D);
  not not_11 (not_11_out, B);
  not not_12 (not_12_out, IN);
  not not_13 (not_13_out, A);
  not not_14 (not_14_out, IN);
  not not_15 (not_15_out, C);
  not not_16 (not_16_out, D);
  not not_17 (not_17_out, IN);
  not not_18 (not_18_out, A);
  not not_19 (not_19_out, IN);
  not not_20 (not_20_out, C);
  not not_21 (not_21_out, B);
  not not_22 (not_22_out, IN);
  not not_23 (not_23_out, D);
  and and_1 (and_1_out, not_1_out, C, IN);
  and and_2 (and_2_out, B, not_2_out, IN);
  and and_3 (and_3_out, not_3_out, B, D, not_4_out);
  and and_4 (and_4_out, A, not_5_out, IN);
  and and_5 (and_5_out, not_6_out, IN);
  and and_6 (and_6_out, not_7_out, C);
  and and_7 (and_7_out, not_8_out, B, not_9_out);
  and and_8 (and_8_out, A, not_10_out);
  and and_9 (and_9_out, A, IN);
  and and_10 (and_10_out, not_11_out, D, not_12_out);
  and and_11 (and_11_out, not_13_out, C, not_14_out);
  and and_12 (and_12_out, B, not_15_out, D, IN);
  and and_13 (and_13_out, A, not_16_out, not_17_out);
  and and_14 (and_14_out, not_18_out, not_19_out);
  and and_15 (and_15_out, not_20_out, D, IN);
  and and_16 (and_16_out, not_21_out, C);
  and and_17 (and_17_out, C, not_22_out);
  and and_18 (and_18_out, A, not_23_out);
  or or_1 (Ap, and_1_out, and_2_out, and_3_out, and_4_out);
  or or_2 (Bp, and_5_out, and_6_out, and_7_out, and_8_out, and_9_out);
  or or_3 (Cp, and_10_out, and_11_out, and_12_out, and_13_out);
  or or_4 (Dp, and_14_out, and_15_out, and_16_out, and_17_out, and_18_out);
endmodule
