// Logisim project Vending.circ as structural Verilog: 6 circuits, main circuit main
module main (
  input  Halt_Enable
);

  wire and_2_out, CLK, Correct, Dime, Done_Testing, Give_Dime, Give_Merch, Give_Nickel, Halt, Nickel,
       not_1_out, not_2_out, not_3_out, Quarter, Sol_Give_Dime, Sol_Give_Merch, Sol_Give_Nickel;
  wire [8:0] counter_1_q, TestNumber;

  Clock clock_1 (.out(CLK));
  not not_1 (not_1_out, Correct);
  and and_1 (Halt, Halt_Enable, not_1_out);
  Inputs inputs_1 (
    .Halt(Halt), .CLK(CLK), .Quarter(Quarter), .Dime(Dime), .Nickel(Nickel), .TestNumber(TestNumber),
    .Done_Testing(Done_Testing));
  // Probe on Quarter
  // Probe on Dime
  // Probe on Nickel
  Vending vending_1 (
    .Quarter(Quarter), .Dime(Dime), .Nickel(Nickel), .CLK(CLK), .Give_Merchandise(Give_Merch),
    .Give_Dime(Give_Dime), .Give_Nickel(Give_Nickel));
  // Probe on Correct
  // Probe on Give_Merch
  // Probe on Sol_Give_Merch
  // Probe on Give_Dime
  // Probe on Sol_Give_Dime
  // Probe on Give_Nickel
  // Probe on Sol_Give_Nickel
  not not_2 (not_2_out, Halt);
  Checker checker_1 (
    .Give_Merch(Give_Merch), .Give_Dime(Give_Dime), .Give_Nickel(Give_Nickel), .TestNumber(TestNumber),
    .Correct(Correct), .Sol_Give_Merch(Sol_Give_Merch), .Sol_Give_Dime(Sol_Give_Dime),
    .Sol_Give_Nickel(Sol_Give_Nickel));
  and and_2 (and_2_out, Correct, not_2_out, not_3_out);
  not not_3 (not_3_out, Done_Testing);
  // Probe on counter_1_q
  Counter #(.width(9), .max('h162), .ongoal("stay")) counter_1 (
    .count(and_2_out), .Q(counter_1_q), .clk(CLK));  // open: load, D, carry, clr

  // Notes on the sheet:
  //   Ardalan Emamjomehkashan
  //   Faustine Yiu 913062973
  //   915356454
  //   Max 354
endmodule

module Vending (
  input  Quarter,
  input  Dime,
  input  Nickel,
  input  CLK,
  output Give_Merchandise,
  output Give_Dime,
  output Give_Nickel
);

  wire and_1_out, and_2_out, and_3_out, and_4_out, and_5_out, and_6_out, and_7_out, and_8_out, and_9_out,
       and_10_out, and_11_out, and_12_out, and_15_out, and_16_out, and_17_out, and_18_out, and_19_out,
       and_20_out, and_21_out, and_22_out, and_23_out, and_24_out, not_1_out, not_2_out, not_3_out,
       not_4_out, not_5_out, not_6_out, not_7_out, not_8_out, not_9_out, not_10_out, not_11_out, not_12_out,
       not_13_out, not_14_out, not_15_out, not_16_out, not_17_out, not_18_out, not_19_out, not_20_out,
       not_21_out, not_22_out, not_23_out, not_24_out, not_25_out, not_26_out, not_27_out, not_28_out,
       not_29_out, not_30_out, not_31_out, or_1_out, or_2_out, or_3_out, x1, x2, x3, x4, x5;

  not not_1 (not_1_out, x1);
  not not_2 (not_2_out, x2);
  not not_3 (not_3_out, x4);
  not not_4 (not_4_out, x5);
  not not_5 (not_5_out, x4);
  not not_6 (not_6_out, x4);
  not not_7 (not_7_out, x5);
  not not_8 (not_8_out, x1);
  not not_9 (not_9_out, x5);
  not not_10 (not_10_out, x1);
  not not_11 (not_11_out, x5);
  not not_12 (not_12_out, x4);
  not not_13 (not_13_out, x2);
  not not_14 (not_14_out, x3);
  not not_15 (not_15_out, x4);
  not not_16 (not_16_out, x5);
  not not_17 (not_17_out, x5);
  not not_18 (not_18_out, x5);
  not not_19 (not_19_out, x4);
  and and_1 (and_1_out, not_1_out, not_2_out, not_3_out);
  and and_2 (and_2_out, not_4_out, not_5_out);
  or or_1 (or_1_out, and_1_out, and_2_out, and_3_out, and_4_out);
  and and_3 (and_3_out, x3, not_6_out);
  and and_4 (and_4_out, x1, x3, not_7_out);
  and and_5 (and_5_out, not_8_out, not_9_out, x4);
  or or_2 (or_2_out, and_5_out, and_6_out, and_7_out);
  and and_6 (and_6_out, not_10_out, x3, not_11_out);
  and and_7 (and_7_out, x2, x5, not_12_out);
  and and_8 (and_8_out, not_13_out, not_14_out, x5, not_15_out);
  and and_9 (and_9_out, x2, not_16_out, x4);
  or or_3 (or_3_out, and_8_out, and_9_out, and_10_out, and_11_out, and_12_out);
  and and_10 (and_10_out, x2, x3, not_17_out);
  and and_11 (and_11_out, x1, not_18_out, x4);
  and and_12 (and_12_out, x1, x3, not_19_out);
  T_Flip_Flop t_ff_1 (.clk(CLK), .T(or_3_out), .Q(x1));  // open: Qn, preset, reset, en
  T_Flip_Flop t_ff_2 (.clk(CLK), .T(or_2_out), .Q(x2));  // open: Qn, preset, reset, en
  T_Flip_Flop t_ff_3 (.clk(CLK), .T(or_1_out), .Q(x3));  // open: Qn, preset, reset, en
  and and_13 (x4, ~Quarter, ~Nickel);  // AND_Gate
  and and_14 (x5, ~Dime, ~Nickel);  // AND_Gate
  not not_20 (not_20_out, x3);
  not not_21 (not_21_out, x4);
  not not_22 (not_22_out, x4);
  not not_23 (not_23_out, x5);
  not not_24 (not_24_out, x4);
  not not_25 (not_25_out, x2);
  not not_26 (not_26_out, x4);
  not not_27 (not_27_out, x4);
  not not_28 (not_28_out, x4);
  not not_29 (not_29_out, x5);
  not not_30 (not_30_out, x4);
  not not_31 (not_31_out, x5);
  and and_15 (and_15_out, x2, not_20_out, x5, not_21_out);
  and and_16 (and_16_out, x1, x5, not_22_out);
  and and_17 (and_17_out, x1, x3, not_23_out, x4);
  and and_18 (and_18_out, x2, x3, x5, not_24_out);
  and and_19 (and_19_out, x1, not_25_out, x5, not_26_out);
  and and_20 (and_20_out, x3, x5, not_27_out);
  and and_21 (and_21_out, x2, x5, not_28_out);
  and and_22 (and_22_out, x1, not_29_out, x4);
  and and_23 (and_23_out, x1, x5, not_30_out);
  and and_24 (and_24_out, x1, x3, not_31_out);
  or or_4 (Give_Nickel, and_15_out, and_16_out, and_17_out);
  or or_5 (Give_Dime, and_18_out, and_19_out);
  or or_6 (Give_Merchandise, and_20_out, and_21_out, and_22_out, and_23_out, and_24_out);

  // Other names for the same wires on the sheet: Quater = Quarter
endmodule

module Inputs (
  input  Halt,
  input  CLK,
  output Quarter,
  output Dime,
  output Nickel,
  output [8:0] TestNumber,
  output Done_Testing
);

  wire not_1_out;

  not not_1 (not_1_out, Halt);
  Counter #(.width(9), .max('h162), .ongoal("stay")) counter_1 (
    .count(not_1_out), .Q(TestNumber), .carry(Done_Testing), .clk(CLK));  // open: load, D, clr
  ROM #(.addrWidth(9), .dataWidth(3)) rom_1 (.addr(TestNumber), .data({Quarter, Dime, Nickel}));  // open: sel

  // Notes on the sheet:
  //   contents of rom_1 (hex, n*v repeats v):
  //   1 0 1 0 1 0 1 0 1 0 1 0 1 0 1 0 1 0 1 0 1 0 2 0 1 0 1 0 1 0 1 0 1 0 4 0 1 0 1 0 1 0 1 0 2 0 1 0 1 0
  //   1 0 1 0 4 0 1 0 1 0 1 0 1 0 2 0 1 0 1 0 1 0 2 0 2 0 1 0 1 0 1 0 2 0 4 0 1 0 1 0 1 0 4 0 1 0 1 0 1 0
  //   1 0 2 0 1 0 1 0 1 0 2 0 2 0 1 0 1 0 1 0 2 0 4 0 1 0 1 0 2 0 2 0 1 0 1 0 2 0 4 0 1 0 1 0 4 0 1 0 1 0
  //   1 0 1 0 2 0 1 0 1 0 1 0 2 0 2 0 1 0 1 0 1 0 2 0 4 0 1 0 1 0 2 0 2 0 1 0 1 0 2 0 4 0 1 0 1 0 2 0 2 0
  //   1 0 2 0 2 0 2 0 1 0 2 0 2 0 4 0 1 0 2 0 4 0 1 0 4 0 1 0 1 0 1 0 1 0 2 0 1 0 1 0 1 0 2 0 2 0 1 0 1 0
  //   1 0 2 0 4 0 1 0 1 0 2 0 2 0 1 0 1 0 2 0 4 0 1 0 1 0 2 0 2 0 1 0 2 0 2 0 2 0 1 0 2 0 2 0 4 0 1 0 2 0
  //   4 0 1 0 1 0 2 0 2 0 1 0 2 0 2 0 2 0 1 0 2 0 2 0 4 0 2 0 2 0 2 0 2 0 2 0 4 0 2 0 4 0 1 0 4 0 2 0 4 0
  //   4 0 4
endmodule

module Checker (
  input  Give_Merch,
  input  Give_Dime,
  input  Give_Nickel,
  input  [8:0] TestNumber,
  output Correct,
  output Sol_Give_Merch,
  output Sol_Give_Dime,
  output Sol_Give_Nickel
);

  ROM #(.addrWidth(9), .dataWidth(3)) rom_1 (
    .addr(TestNumber), .data({Sol_Give_Merch, Sol_Give_Dime, Sol_Give_Nickel}));  // open: sel
  Comparator #(.width(3)) comparator_1 (
    .a({Sol_Give_Merch, Sol_Give_Dime, Sol_Give_Nickel}), .b({Give_Merch, Give_Dime, Give_Nickel}),
    .eq(Correct));  // open: gt, lt

  // Other names for the same wires on the sheet: Solution[2:0] = {Sol_Give_Merch, Sol_Give_Dime, Sol_Give_Nickel};
  //   Your_Answer[2:0] = {Give_Merch, Give_Dime, Give_Nickel}

  // Notes on the sheet:
  //   contents of rom_1 (hex, n*v repeats v):
  //   10*0 4 11*0 5 11*0 7 9*0 4 9*0 7 9*0 4 9*0 5 9*0 7 7*0 6 9*0 4 9*0 5 9*0 7 7*0 4 7*0 7 5*0 5 9*0 4
  //   9*0 5 9*0 7 7*0 4 7*0 7 7*0 4 7*0 5 7*0 7 5*0 6 0 0 0 4 9*0 4 9*0 5 9*0 7 7*0 4 7*0 7 7*0 4 7*0 5
  //   7*0 7 5*0 6 7*0 4 7*0 5 7*0 7 5*0 4 5*0 7 0 0 0 5 0 0 0 4 0 0 0 5 0 0 0 7
endmodule

module xyz (
  input  x1,
  input  x2,
  input  x3,
  input  x4,
  input  x5,
  output x,
  output y,
  output z
);

  wire and_1_out, and_2_out, and_3_out, and_4_out, and_5_out, and_6_out, and_7_out, and_8_out, and_9_out,
       and_10_out, and_11_out, and_12_out, not_1_out, not_2_out, not_3_out, not_4_out, not_5_out, not_6_out,
       not_7_out, not_8_out, not_9_out, not_10_out, not_11_out, not_12_out, not_13_out, not_14_out,
       not_15_out, not_16_out, not_17_out, not_18_out, not_19_out;

  not not_1 (not_1_out, x1);
  not not_2 (not_2_out, x5);
  not not_3 (not_3_out, x1);
  not not_4 (not_4_out, x5);
  not not_5 (not_5_out, x4);
  not not_6 (not_6_out, x1);
  not not_7 (not_7_out, x2);
  not not_8 (not_8_out, x4);
  not not_9 (not_9_out, x5);
  not not_10 (not_10_out, x4);
  not not_11 (not_11_out, x4);
  not not_12 (not_12_out, x5);
  not not_13 (not_13_out, x2);
  not not_14 (not_14_out, x3);
  not not_15 (not_15_out, x4);
  not not_16 (not_16_out, x5);
  not not_17 (not_17_out, x5);
  not not_18 (not_18_out, x5);
  not not_19 (not_19_out, x4);
  and and_1 (and_1_out, not_1_out, not_2_out, x4);
  and and_2 (and_2_out, not_3_out, x3, not_4_out);
  and and_3 (and_3_out, x2, x5, not_5_out);
  and and_4 (and_4_out, not_6_out, not_7_out, not_8_out);
  and and_5 (and_5_out, not_9_out, not_10_out);
  and and_6 (and_6_out, x3, not_11_out);
  and and_7 (and_7_out, x1, x3, not_12_out);
  and and_8 (and_8_out, not_13_out, not_14_out, x5, not_15_out);
  and and_9 (and_9_out, x2, not_16_out, x4);
  and and_10 (and_10_out, x2, x3, not_17_out);
  and and_11 (and_11_out, x1, not_18_out, x4);
  and and_12 (and_12_out, x1, x3, not_19_out);
  or or_1 (x, and_1_out, and_2_out, and_3_out);
  or or_2 (y, and_4_out, and_5_out, and_6_out, and_7_out);
  or or_3 (z, and_8_out, and_9_out, and_10_out, and_11_out, and_12_out);
endmodule

module MDN (
  input  x1,
  input  x2,
  input  x3,
  input  x4,
  input  x5,
  output Give_Merchandise,
  output Give_Dime,
  output Give_Nickel
);

  wire and_1_out, and_2_out, and_3_out, and_4_out, and_5_out, and_6_out, and_7_out, and_8_out, and_9_out,
       and_10_out, not_1_out, not_2_out, not_3_out, not_4_out, not_5_out, not_6_out, not_7_out, not_8_out,
       not_9_out, not_10_out, not_11_out, not_12_out;

  not not_1 (not_1_out, x3);
  not not_2 (not_2_out, x4);
  not not_3 (not_3_out, x4);
  not not_4 (not_4_out, x5);
  not not_5 (not_5_out, x4);
  not not_6 (not_6_out, x2);
  not not_7 (not_7_out, x4);
  not not_8 (not_8_out, x4);
  not not_9 (not_9_out, x4);
  not not_10 (not_10_out, x5);
  not not_11 (not_11_out, x4);
  not not_12 (not_12_out, x5);
  and and_1 (and_1_out, x2, not_1_out, x5, not_2_out);
  and and_2 (and_2_out, x1, x5, not_3_out);
  and and_3 (and_3_out, x1, x3, not_4_out, x4);
  and and_4 (and_4_out, x2, x3, x5, not_5_out);
  and and_5 (and_5_out, x1, not_6_out, x5, not_7_out);
  and and_6 (and_6_out, x3, x5, not_8_out);
  and and_7 (and_7_out, x2, x5, not_9_out);
  and and_8 (and_8_out, x1, not_10_out, x4);
  and and_9 (and_9_out, x1, x5, not_11_out);
  and and_10 (and_10_out, x1, x3, not_12_out);
  or or_1 (Give_Merchandise, and_1_out, and_2_out, and_3_out);
  or or_2 (Give_Dime, and_4_out, and_5_out);
  or or_3 (Give_Nickel, and_6_out, and_7_out, and_8_out, and_9_out, and_10_out);
endmodule
